// Logisim project AddressBus.circ as structural Verilog: 1 circuit, main circuit main
module main (
);

  wire and_1_out, and_2_out, and_3_out, and_4_out, and_5_out, and_6_out, and_7_out, and_8_out, and_9_out,
       and_10_out, and_11_out, and_12_out, and_13_out, and_14_out, and_15_out, and_16_out, and_17_out,
       and_18_out, and_19_out, dipswitch_1_p1, dipswitch_1_p2, dipswitch_1_p3, dipswitch_1_p4,
       dipswitch_1_p5, dipswitch_1_p6, dipswitch_1_p7, dipswitch_1_p8, dipswitch_1_p9, dipswitch_1_p10,
       dipswitch_1_p11, dipswitch_1_p12, dipswitch_2_p1, dipswitch_2_p2, dipswitch_2_p3, dipswitch_2_p4,
       framebuffer, not_2_out, not_3_out, not_4_out, not_5_out, not_6_out, not_7_out, not_8_out, not_9_out,
       not_10_out, not_11_out, not_12_out, not_14_out, not_15_out, not_17_out, or_1_out, RAM, RNG, ROM;

  not not_1 (ROM, dipswitch_1_p1);
  LED led_1 (.in(ROM));
  LED led_2 (.in(RNG));
  LED led_3 (.in(framebuffer));
  LED led_4 (.in(RAM));
  LED led_5 (.in(dipswitch_1_p1));
  LED led_6 (.in(dipswitch_1_p2));
  LED led_7 (.in(dipswitch_1_p3));
  LED led_8 (.in(dipswitch_1_p4));
  LED led_9 (.in(dipswitch_1_p5));
  // DipSwitch dipswitch_1: pin names not known; wires that end beside it: dipswitch_1_p1, dipswitch_1_p2, dipswitch_1_p3, dipswitch_1_p4, dipswitch_1_p5, dipswitch_1_p6, dipswitch_1_p7, dipswitch_1_p8, dipswitch_1_p9, dipswitch_1_p10, dipswitch_1_p11, dipswitch_1_p12
  LED led_10 (.in(dipswitch_1_p6));
  LED led_11 (.in(dipswitch_1_p7));
  LED led_12 (.in(dipswitch_1_p8));
  LED led_13 (.in(dipswitch_1_p9));
  LED led_14 (.in(dipswitch_1_p10));
  LED led_15 (.in(dipswitch_1_p11));
  LED led_16 (.in(dipswitch_1_p12));
  // DipSwitch dipswitch_2: pin names not known; wires that end beside it: dipswitch_2_p1, dipswitch_2_p2, dipswitch_2_p3, dipswitch_2_p4
  LED led_17 (.in(dipswitch_2_p1));
  LED led_18 (.in(dipswitch_2_p2));
  LED led_19 (.in(dipswitch_2_p3));
  LED led_20 (.in(dipswitch_2_p4));
  not not_2 (not_2_out, dipswitch_1_p1);
  and and_1 (and_1_out, not_2_out, not_3_out);
  not not_3 (not_3_out, dipswitch_1_p2);
  not not_4 (not_4_out, dipswitch_1_p3);
  and and_2 (and_2_out, not_4_out, not_5_out);
  not not_5 (not_5_out, dipswitch_1_p4);
  not not_6 (not_6_out, dipswitch_1_p5);
  and and_3 (and_3_out, not_6_out, not_7_out);
  not not_7 (not_7_out, dipswitch_1_p6);
  not not_8 (not_8_out, dipswitch_1_p7);
  and and_4 (and_4_out, not_8_out, not_9_out);
  not not_9 (not_9_out, dipswitch_1_p8);
  and and_5 (and_5_out, dipswitch_1_p9, dipswitch_1_p10);
  and and_6 (and_6_out, dipswitch_1_p11, dipswitch_1_p12);
  and and_7 (and_7_out, dipswitch_2_p1, dipswitch_2_p2);
  not not_10 (not_10_out, dipswitch_1_p5);
  not not_11 (not_11_out, dipswitch_1_p6);
  not not_12 (not_12_out, dipswitch_1_p7);
  and and_8 (and_8_out, and_1_out, and_2_out);
  and and_9 (and_9_out, and_3_out, and_4_out);
  and and_10 (and_10_out, and_5_out, and_6_out);
  and and_11 (and_11_out, not_11_out, dipswitch_1_p7);
  and and_12 (and_12_out, dipswitch_1_p6, not_12_out);
  and and_13 (and_13_out, and_8_out, and_9_out);
  and and_14 (and_14_out, and_10_out, and_7_out);
  and and_15 (and_15_out, not_10_out, or_1_out);
  or or_1 (or_1_out, and_11_out, and_12_out);
  and and_16 (and_16_out, and_8_out, and_15_out);
  not not_13 (RNG, and_17_out);
  and and_17 (and_17_out, and_13_out, and_14_out);
  not not_14 (not_14_out, dipswitch_1_p1);
  not not_15 (not_15_out, and_16_out);
  not not_16 (framebuffer, and_16_out);
  not not_17 (not_17_out, and_17_out);
  and and_18 (and_18_out, not_14_out, not_15_out);
  and and_19 (and_19_out, not_17_out, and_18_out);
  not not_18 (RAM, and_19_out);

  // Notes on the sheet:
  //   High Byte Off
  //   RNG
endmodule
