// Logisim project AddressBusV3.circ as structural Verilog: 1 circuit, main circuit main
module main (
);

  wire A00, A01, A02, A03, A04, A05, A06, A07, A08, A09, A10, A11, A12, A13, A14, A15, FRMBUF, n7402_1_pin1,
       n7402_1_pin4, n7402_1_pin10, n7402_1_pin13, n7408_1_pin3, n7408_1_pin6, n7408_1_pin11, n7408_1_pin12,
       n7408_2_pin3, n7408_2_pin6, n7408_2_pin8, n7408_2_pin11, n7408_2_pin13, n7408_3_pin3, n7414_1_pin2,
       n7414_1_pin4, n7414_1_pin6, n7414_2_pin9, n7421_1_pin6, n7421_1_pin8, n7421_1_pin13, RAM, RNG, ROM;

  LED led_1 (.in(A00));
  LED led_2 (.in(A00));
  LED led_3 (.in(A01));
  LED led_4 (.in(A01));
  LED led_5 (.in(A02));
  LED led_6 (.in(A02));
  LED led_7 (.in(A03));
  LED led_8 (.in(A03));
  LED led_9 (.in(A04));
  LED led_10 (.in(A04));
  LED led_11 (.in(A05));
  LED led_12 (.in(A05));
  LED led_13 (.in(A06));
  LED led_14 (.in(A06));
  LED led_15 (.in(A07));
  LED led_16 (.in(A07));
  LED led_17 (.in(A08));
  LED led_18 (.in(A08));
  LED led_19 (.in(A09));
  LED led_20 (.in(A10));
  LED led_21 (.in(A10));
  LED led_22 (.in(A11));
  LED led_23 (.in(A11));
  LED led_24 (.in(A12));
  LED led_25 (.in(A12));
  LED led_26 (.in(A13));
  LED led_27 (.in(A13));
  LED led_28 (.in(A14));
  LED led_29 (.in(A14));
  LED led_30 (.in(A15));
  LED led_31 (.in(RNG));
  LED led_32 (.in(RNG));
  LED led_33 (.in(ROM));
  LED led_34 (.in(ROM));
  LED led_35 (.in(FRMBUF));
  LED led_36 (.in(FRMBUF));
  LED led_37 (.in(RAM));
  LED led_38 (.in(RAM));
  // DipSwitch dipswitch_1: pin names not known; wires that end beside it: A15, A14, A13, A12, A11, A10, A09, A08, A07, A06, A05, A04
  // DipSwitch dipswitch_2: pin names not known; wires that end beside it: A03, A02, A01, A00
  _7402 u_7402_1 (
    .pin1(n7402_1_pin1), .pin2(A15), .pin3(A14), .pin4(n7402_1_pin4), .pin5(A13), .pin6(A12),
    .pin13(n7402_1_pin13), .pin12(A08), .pin11(A09), .pin10(n7402_1_pin10), .pin9(A10), .pin8(A11));
  _7421 u_7421_1 (
    .pin1(A07), .pin2(A06), .pin4(A05), .pin5(A04), .pin6(n7421_1_pin6), .pin13(n7421_1_pin13), .pin12(A02),
    .pin10(A03), .pin9(n7421_1_pin6), .pin8(n7421_1_pin8));  // open: pin3, pin11
  _7414 u_7414_1 (
    .pin1(A11), .pin2(n7414_1_pin2), .pin3(A10), .pin4(n7414_1_pin4), .pin5(A09), .pin6(n7414_1_pin6));  // open: pin13, pin12, pin11, pin10, pin9, pin8
  _7408 u_7408_1 (
    .pin1(n7402_1_pin1), .pin2(n7402_1_pin4), .pin3(n7408_1_pin3), .pin4(n7402_1_pin13),
    .pin5(n7402_1_pin10), .pin6(n7408_1_pin6), .pin13(n7421_1_pin8), .pin12(n7408_1_pin12),
    .pin11(n7408_1_pin11), .pin10(n7408_1_pin3), .pin9(n7408_1_pin6), .pin8(n7408_1_pin12));
  _7408 u_7408_2 (
    .pin1(A10), .pin2(n7414_1_pin6), .pin3(n7408_2_pin3), .pin4(A09), .pin5(n7414_1_pin4),
    .pin6(n7408_2_pin6), .pin13(n7408_2_pin13), .pin12(n7414_1_pin2), .pin11(n7408_2_pin11),
    .pin10(n7408_2_pin11), .pin9(n7408_1_pin3), .pin8(n7408_2_pin8));
  _7414 u_7414_2 (
    .pin1(n7408_1_pin11), .pin2(RNG), .pin3(A15), .pin4(ROM), .pin5(n7408_2_pin8), .pin6(FRMBUF),
    .pin9(n7414_2_pin9), .pin8(RAM));  // open: pin13, pin12, pin11, pin10
  _7408 u_7408_3 (
    .pin1(FRMBUF), .pin2(ROM), .pin3(n7408_3_pin3), .pin4(n7408_3_pin3), .pin5(RNG), .pin6(n7414_2_pin9));  // open: pin13, pin12, pin11, pin10, pin9, pin8
  _7432 u_7432_1 (
    .pin1(n7408_2_pin3), .pin2(n7408_2_pin6), .pin3(n7408_2_pin13));  // open: pin4, pin5, pin6, pin13, pin12, pin11, pin10, pin9, pin8
  // also tied to VCC on the sheet: n7421_1_pin13
endmodule
