// Logisim project AddressBusV9_gates.circ as structural Verilog: 1 circuit, main circuit main
module main (
);

  wire A00, A01, A02, A03, A04, A05, A06, A07, A08, A09, A10, A11, A11_CLEAR, A12, A13, A14, A15, and_2_out,
       and_3_out, and_7_out, and_8_out, and_11_out, fastclock, FRMBUF, FRMBUF_CS, HB_HN_CLEAR, HB_LN_CLEAR,
       HB_LN_FBUF, INTERRUPT, LB_HN_SET, LB_LN_RNG, not_1_out, not_2_out, not_3_out, not_4_out, not_5_out,
       not_6_out, not_7_out, not_8_out, not_9_out, not_10_out, not_13_out, not_14_out, not_15_out, or_2_out,
       RAM, RAM_CS, RNG, RNG_CS, ROM_CS, slowclock1, z80Clock;

  LED led_1 (.in(A00));
  LED led_2 (.in(A01));
  LED led_3 (.in(A02));
  LED led_4 (.in(A03));
  LED led_5 (.in(A04));
  LED led_6 (.in(A05));
  LED led_7 (.in(A06));
  LED led_8 (.in(A07));
  LED led_9 (.in(A08));
  LED led_10 (.in(A09));
  LED led_11 (.in(A10));
  LED led_12 (.in(A11));
  LED led_13 (.in(A12));
  LED led_14 (.in(A13));
  LED led_15 (.in(A14));
  LED led_16 (.in(A15));
  Button button_1 (.out(slowclock1));
  Clock clock_1 (.out(fastclock));
  LED led_17 (.in(RNG));
  LED led_18 (.in(A15));
  LED led_19 (.in(FRMBUF));
  LED led_20 (.in(RAM));
  LED led_21 (.in(z80Clock));
  LED led_22 (.in(RNG_CS));
  LED led_23 (.in(ROM_CS));
  LED led_24 (.in(FRMBUF_CS));
  LED led_25 (.in(RAM_CS));
  LED led_26 (.in(INTERRUPT));
  // DipSwitch dipswitch_1: pin names not known; wires that end beside it: A15, A14, A13, A12, A11, A10, A09, A08, A07, A06, A05, A04
  // DipSwitch dipswitch_2: pin names not known; wires that end beside it: A03, A02, A01, A00
  not not_1 (not_1_out, A15);
  not not_2 (not_2_out, A14);
  not not_3 (not_3_out, A13);
  not not_4 (not_4_out, A12);
  not not_5 (not_5_out, A10);
  not not_6 (not_6_out, A09);
  not not_7 (not_7_out, A11);
  not not_8 (not_8_out, A10);
  not not_9 (not_9_out, A09);
  not not_10 (not_10_out, A08);
  and and_1 (HB_HN_CLEAR, not_1_out, not_2_out, not_3_out, not_4_out);
  and and_2 (and_2_out, not_5_out, A09);
  or or_1 (HB_LN_FBUF, and_2_out, and_3_out);
  and and_3 (and_3_out, A10, not_6_out);
  not not_11 (A11_CLEAR, A11);
  and and_4 (HB_LN_CLEAR, not_7_out, not_8_out, not_9_out, not_10_out);
  and and_5 (LB_HN_SET, A07, A06, A05, A04);
  and and_6 (LB_LN_RNG, A03, A02);
  or or_2 (or_2_out, A15, RAM);
  and and_7 (and_7_out, or_2_out, fastclock);
  not not_12 (ROM_CS, A15);
  nand nand_1 (RAM_CS, RAM, z80Clock);
  and and_8 (and_8_out, HB_LN_FBUF, A11_CLEAR);
  and and_9 (RNG, HB_HN_CLEAR, HB_LN_CLEAR, LB_HN_SET, LB_LN_RNG);
  not not_13 (not_13_out, A15);
  not not_14 (not_14_out, FRMBUF);
  not not_15 (not_15_out, RNG);
  or or_3 (z80Clock, and_7_out, slowclock1);
  and and_10 (FRMBUF, and_8_out, HB_HN_CLEAR);
  and and_11 (and_11_out, not_13_out, not_14_out);
  and and_12 (RAM, and_11_out, not_15_out);

  // Other names for the same wires on the sheet: HB_HN_ROM = A15; ROM = A15

  // Notes on the sheet:
  //   HB = High Byte
  //   LB = Low Byte
  //   HN = High Nibble
  //   LN = Low Nibble
endmodule
