// Logisim project AddressBusV9_gates_bus.circ as structural Verilog: 1 circuit, main circuit main
module main (
);

  wire A11_CLEAR, and_3_out, and_4_out, and_7_out, and_8_out, and_11_out, fastclock, FRMBUF, HB_HN_CLEAR,
       HB_LN_CLEAR, HB_LN_FBUF, LB_HN_SET, LB_LN_RNG, mainclock, not_1_out, not_2_out, not_3_out, not_4_out,
       not_5_out, not_6_out, not_7_out, not_10_out, not_11_out, or_2_out, RAM, RAM_CS, RNG, ROM, ROM_CS,
       slowclock1;
  wire [14:0] undriven;

  Button button_1 (.out(slowclock1));
  Clock clock_1 (.out(fastclock));
  LED led_1 (.in(RNG));
  LED led_2 (.in(ROM));
  LED led_3 (.in(FRMBUF));
  LED led_4 (.in(RAM));
  LED led_5 (.in(mainclock));
  LED led_6 (.in(ROM_CS));
  LED led_7 (.in(RAM_CS));
  // DipSwitch #(.number(16)) dipswitch_1: pin names not known
  Hex_Digit_Display hex_digit_display_1 (.value({ROM, undriven[14:12]}));  // open: dp
  Hex_Digit_Display hex_digit_display_2 (.value(undriven[11:8]));  // open: dp
  not not_1 (not_1_out, undriven[12]);
  not not_2 (not_2_out, undriven[13]);
  not not_3 (not_3_out, undriven[14]);
  not not_4 (not_4_out, ROM);
  not not_5 (not_5_out, undriven[8]);
  not not_6 (not_6_out, undriven[9]);
  not not_7 (not_7_out, undriven[10]);
  not not_8 (A11_CLEAR, undriven[11]);
  Hex_Digit_Display hex_digit_display_3 (.value(undriven[7:4]));  // open: dp
  Hex_Digit_Display hex_digit_display_4 (.value(undriven[3:0]));  // open: dp
  and and_1 (HB_HN_CLEAR, not_1_out, not_2_out, not_3_out, not_4_out);
  and and_2 (HB_LN_CLEAR, not_5_out, not_6_out, not_7_out, A11_CLEAR);
  and and_3 (and_3_out, not_6_out, undriven[10]);
  and and_4 (and_4_out, undriven[9], not_7_out);
  and and_5 (LB_HN_SET, undriven[4], undriven[5], undriven[6], undriven[7]);
  and and_6 (LB_LN_RNG, undriven[2], undriven[3]);
  or or_1 (HB_LN_FBUF, and_3_out, and_4_out);
  or or_2 (or_2_out, ROM, RAM);
  not not_9 (ROM_CS, ROM);
  and and_7 (and_7_out, or_2_out, fastclock);
  nand nand_1 (RAM_CS, RAM, mainclock);
  and and_8 (and_8_out, HB_LN_FBUF, A11_CLEAR);
  and and_9 (RNG, HB_HN_CLEAR, HB_LN_CLEAR, LB_HN_SET, LB_LN_RNG);
  not not_10 (not_10_out, FRMBUF);
  not not_11 (not_11_out, RNG);
  or or_3 (mainclock, and_7_out, slowclock1);
  and and_10 (FRMBUF, and_8_out, HB_HN_CLEAR);
  and and_11 (and_11_out, ROM_CS, not_10_out);
  and and_12 (RAM, and_11_out, not_11_out);

  // Notes on the sheet:
  //   HB = High Byte
  //   LB = Low Byte
  //   HN = High Nibble
  //   LN = Low Nibble
endmodule
