// Logisim project AddressBusV9_ttl.circ as structural Verilog: 1 circuit, main circuit main
module main (
);

  wire fastClock, FRMBUF, mainClock, n7408_1_pin3, n7408_1_pin6, n7408_1_pin11, n7408_1_pin13, n7408_2_pin6,
       n7414_1_pin4, n7414_1_pin6, n7414_1_pin8, n7414_1_pin10, n7414_1_pin12, n7414_2_pin2, n7414_2_pin4,
       n7421_1_pin6, n7421_1_pin8, n7421_1_pin9, n7421_1_pin10, n7421_2_pin6, n7421_2_pin10, n7432_1_pin5,
       n7432_1_pin6, n7432_1_pin13, RAM_CS, RNG, ROM_CS, slowClock, undriven_2;
  wire [15:0] undriven;

  Clock clock_1 (.out(fastClock));
  Button button_1 (.out(slowClock));
  LED led_1 (.in(RNG));
  LED led_2 (.in(FRMBUF));
  LED led_3 (.in(mainClock));
  LED led_4 (.in(ROM_CS));
  LED led_5 (.in(RAM_CS));
  _7414 #(.ShowInternalStructure("true")) u_7414_1 (
    .pin1(undriven[15]), .pin2(ROM_CS), .pin3(undriven[11]), .pin4(n7414_1_pin4), .pin5(undriven[10]),
    .pin6(n7414_1_pin6), .pin13(undriven[14]), .pin12(n7414_1_pin12), .pin11(undriven[13]),
    .pin10(n7414_1_pin10), .pin9(undriven[12]), .pin8(n7414_1_pin8));
  // DipSwitch #(.number(16)) dipswitch_1: pin names not known
  Hex_Digit_Display hex_digit_display_1 (.value(undriven[15:12]));  // open: dp
  Hex_Digit_Display hex_digit_display_2 (.value(undriven[11:8]));  // open: dp
  Hex_Digit_Display hex_digit_display_3 (.value(undriven[7:4]), .dp(undriven_2));
  Hex_Digit_Display hex_digit_display_4 (.value(undriven[7:4]), .dp(undriven_2));
  _7421 #(.ShowInternalStructure("true")) u_7421_1 (
    .pin1(ROM_CS), .pin2(n7414_1_pin12), .pin4(n7414_1_pin10), .pin5(n7414_1_pin8), .pin6(n7421_1_pin6),
    .pin13(n7414_1_pin4), .pin12(n7414_1_pin6), .pin10(n7421_1_pin10), .pin9(n7421_1_pin9),
    .pin8(n7421_1_pin8));  // open: pin3, pin11
  Hex_Digit_Display hex_digit_display_5 (.value(undriven[3:0]));  // open: dp
  _7414 #(.ShowInternalStructure("true")) u_7414_2 (
    .pin1(FRMBUF), .pin2(n7414_2_pin2), .pin3(RNG), .pin4(n7414_2_pin4), .pin13(undriven[9]),
    .pin12(n7421_1_pin10), .pin11(undriven[8]), .pin10(n7421_1_pin9));  // open: pin5, pin6, pin9, pin8
  _7408 #(.ShowInternalStructure("true")) u_7408_1 (
    .pin1(n7414_1_pin6), .pin2(undriven[9]), .pin3(n7408_1_pin3), .pin4(undriven[10]), .pin5(n7421_1_pin10),
    .pin6(n7408_1_pin6), .pin13(n7408_1_pin13), .pin12(n7414_1_pin4), .pin11(n7408_1_pin11),
    .pin10(n7408_1_pin11), .pin9(n7421_1_pin6), .pin8(FRMBUF));
  _7432 #(.ShowInternalStructure("true")) u_7432_1 (
    .pin1(n7408_1_pin3), .pin2(n7408_1_pin6), .pin3(n7408_1_pin13), .pin4(undriven[15]), .pin5(n7432_1_pin5),
    .pin6(n7432_1_pin6), .pin13(n7432_1_pin13), .pin12(slowClock), .pin11(mainClock));  // open: pin10, pin9, pin8
  _7421 #(.ShowInternalStructure("true")) u_7421_2 (
    .pin1(undriven[7]), .pin2(undriven[6]), .pin4(undriven[5]), .pin5(undriven[4]), .pin6(n7421_2_pin6),
    .pin13(n7421_1_pin6), .pin12(n7421_1_pin8), .pin10(n7421_2_pin10), .pin9(n7421_2_pin6), .pin8(RNG));  // open: pin3, pin11
  _7400 #(.ShowInternalStructure("true")) u_7400_1 (
    .pin1(n7432_1_pin5), .pin2(mainClock), .pin3(RAM_CS));  // open: pin4, pin5, pin6, pin13, pin12, pin11, pin10, pin9, pin8
  _7408 #(.ShowInternalStructure("true")) u_7408_2 (
    .pin1(undriven[3]), .pin2(undriven[2]), .pin3(n7421_2_pin10), .pin4(n7414_2_pin2), .pin5(n7414_2_pin4),
    .pin6(n7408_2_pin6), .pin13(n7432_1_pin6), .pin12(fastClock), .pin11(n7432_1_pin13),
    .pin10(n7408_2_pin6), .pin9(ROM_CS), .pin8(n7432_1_pin5));
endmodule
