// Logisim project m6502MemoryMap.circ as structural Verilog: 1 circuit, main circuit main
module main (
);

  wire A15, and_1_out, and_2_out, and_3_out, and_4_out, and_5_out, and_6_out, and_7_out, and_8_out,
       and_9_out, and_10_out, and_11_out, and_12_out, and_15_out, and_16_out, and_17_out, and_18_out,
       and_19_out, and_20_out, and_21_out, and_22_out, and_23_out, and_24_out, and_25_out, and_26_out,
       and_27_out, and_28_out, and_29_out, and_30_out, clock, dipswitch_1_p1, dipswitch_1_p2, dipswitch_1_p3,
       dipswitch_1_p4, dipswitch_1_p5, dipswitch_1_p6, dipswitch_1_p7, dipswitch_1_p8, dipswitch_2_p1,
       dipswitch_2_p2, dipswitch_2_p3, dipswitch_2_p4, dipswitch_2_p5, dipswitch_2_p6, dipswitch_2_p7,
       dipswitch_2_p8, dipswitch_3_p1, dipswitch_3_p2, dipswitch_3_p3, dipswitch_3_p4, dipswitch_3_p5,
       dipswitch_3_p6, dipswitch_4_p1, dipswitch_4_p2, dipswitch_4_p3, dipswitch_4_p4, dipswitch_4_p5,
       dipswitch_4_p6, dipswitch_4_p7, dipswitch_4_p8, dipswitch_5_p1, dipswitch_5_p2, dipswitch_5_p3,
       dipswitch_5_p4, dipswitch_5_p5, dipswitch_5_p6, dipswitch_5_p7, dipswitch_6_p1, dipswitch_6_p2,
       dipswitch_6_p3, dipswitch_6_p4, framebuffer, highbyte, highbyteoff, highbyteoffWrong, highnibbleoff,
       nor_1_out, nor_2_out, nor_3_out, nor_4_out, nor_5_out, nor_6_out, not_1_out, not_2_out, not_3_out,
       not_4_out, not_5_out, not_6_out, not_7_out, not_8_out, not_9_out, not_10_out, not_11_out, not_12_out,
       not_13_out, not_14_out, not_15_out, not_16_out, not_17_out, not_18_out, not_19_out, not_20_out,
       not_21_out, not_22_out, or_1_out, rng;

  // DipSwitch dipswitch_1: pin names not known; wires that end beside it: dipswitch_1_p1, dipswitch_1_p2, dipswitch_1_p3, dipswitch_1_p4, dipswitch_1_p5, dipswitch_1_p6, dipswitch_1_p7, dipswitch_1_p8
  Clock clock_1 (.out(clock));
  // DipSwitch dipswitch_2: pin names not known; wires that end beside it: dipswitch_2_p1, dipswitch_2_p2, dipswitch_2_p3, dipswitch_2_p4, dipswitch_2_p5, dipswitch_2_p6, dipswitch_2_p7, dipswitch_2_p8, clock
  // Digital_Oscilloscope digital_oscilloscope_1: pin names not known; wires that end beside it: clock, highbyte, framebuffer
  // DipSwitch dipswitch_3: pin names not known; wires that end beside it: dipswitch_3_p1, dipswitch_3_p2, dipswitch_3_p3, dipswitch_3_p4, dipswitch_3_p5, dipswitch_3_p6
  not not_1 (not_1_out, dipswitch_1_p1);
  and and_1 (and_1_out, not_1_out, not_2_out);
  not not_2 (not_2_out, dipswitch_1_p2);
  not not_3 (not_3_out, dipswitch_1_p3);
  and and_2 (and_2_out, not_3_out, not_4_out);
  not not_4 (not_4_out, dipswitch_1_p4);
  not not_5 (not_5_out, dipswitch_1_p5);
  and and_3 (and_3_out, not_5_out, not_6_out);
  not not_6 (not_6_out, dipswitch_1_p6);
  not not_7 (not_7_out, dipswitch_1_p7);
  and and_4 (and_4_out, not_7_out, not_8_out);
  not not_8 (not_8_out, dipswitch_1_p8);
  and and_5 (and_5_out, dipswitch_3_p1, dipswitch_3_p2);
  and and_6 (and_6_out, dipswitch_3_p3, dipswitch_3_p4);
  and and_7 (and_7_out, dipswitch_3_p5, dipswitch_3_p6);
  nor nor_1 (nor_1_out, dipswitch_2_p1, dipswitch_2_p2);
  and and_8 (and_8_out, and_1_out, and_2_out);
  and and_9 (and_9_out, and_3_out, and_4_out);
  and and_10 (and_10_out, and_5_out, and_6_out);
  not not_9 (not_9_out, A15);
  and and_11 (and_11_out, not_9_out, not_10_out);
  not not_10 (not_10_out, framebuffer);
  and and_12 (and_12_out, highbyteoff, rng);
  nor nor_2 (nor_2_out, nor_1_out, dipswitch_2_p3);
  and and_13 (highbyteoff, and_8_out, and_9_out);
  not not_11 (not_11_out, and_12_out);
  nor nor_3 (nor_3_out, nor_2_out, dipswitch_2_p4);
  nor nor_4 (nor_4_out, nor_3_out, dipswitch_2_p5);
  and and_14 (rng, and_10_out, and_7_out);
  and and_15 (and_15_out, and_11_out, not_11_out);
  LED led_1 (.in(and_15_out));
  nor nor_5 (nor_5_out, nor_4_out, dipswitch_2_p6);
  // DipSwitch dipswitch_4: pin names not known; wires that end beside it: dipswitch_4_p1, dipswitch_4_p2, dipswitch_4_p3, dipswitch_4_p4, dipswitch_4_p5, dipswitch_4_p6, dipswitch_4_p7, dipswitch_4_p8
  // DipSwitch dipswitch_5: pin names not known; wires that end beside it: dipswitch_5_p1, dipswitch_5_p2, dipswitch_5_p3, dipswitch_5_p4, dipswitch_5_p5, dipswitch_5_p6, dipswitch_5_p7
  nor nor_6 (nor_6_out, nor_5_out, dipswitch_2_p7);
  // DipSwitch dipswitch_6: pin names not known; wires that end beside it: dipswitch_6_p1, dipswitch_6_p2, dipswitch_6_p3, dipswitch_6_p4
  // DipSwitch dipswitch_7: pin names not known; wires that end beside it: A15
  nor nor_7 (highbyte, nor_6_out, dipswitch_2_p8);
  and and_16 (and_16_out, dipswitch_4_p1, dipswitch_4_p2);
  and and_17 (and_17_out, dipswitch_4_p3, dipswitch_4_p4);
  and and_18 (and_18_out, dipswitch_4_p5, dipswitch_4_p6);
  and and_19 (and_19_out, dipswitch_4_p7, dipswitch_4_p8);
  not not_12 (not_12_out, dipswitch_5_p1);
  and and_20 (and_20_out, not_12_out, not_13_out);
  not not_13 (not_13_out, dipswitch_5_p2);
  not not_14 (not_14_out, dipswitch_5_p3);
  and and_21 (and_21_out, not_14_out, not_15_out);
  not not_15 (not_15_out, dipswitch_5_p4);
  not not_16 (not_16_out, dipswitch_5_p5);
  not not_17 (not_17_out, dipswitch_5_p6);
  and and_22 (and_22_out, not_17_out, dipswitch_5_p7);
  and and_23 (and_23_out, dipswitch_5_p6, not_18_out);
  not not_18 (not_18_out, dipswitch_5_p7);
  not not_19 (not_19_out, dipswitch_6_p1);
  not not_20 (not_20_out, dipswitch_6_p2);
  not not_21 (not_21_out, dipswitch_6_p3);
  not not_22 (not_22_out, dipswitch_6_p4);
  and and_24 (and_24_out, and_16_out, and_17_out);
  and and_25 (and_25_out, and_18_out, and_19_out);
  and and_26 (and_26_out, and_20_out, and_21_out);
  or or_1 (or_1_out, and_22_out, and_23_out);
  and and_27 (and_27_out, not_19_out, not_20_out);
  and and_28 (and_28_out, not_21_out, not_22_out);
  and and_29 (and_29_out, and_24_out, and_25_out);
  and and_30 (and_30_out, not_16_out, or_1_out);
  and and_31 (highnibbleoff, and_27_out, and_28_out);
  not not_23 (highbyteoffWrong, and_29_out);
  and and_32 (framebuffer, and_26_out, and_30_out);
endmodule
